# Fritzing sketch schema (saved by Fritzing 1.0.6)
circuit board: 7cm x 5cm

parts:
  Pad44 = Pad [width=3.5794580238945084 height=1.453889245399575 connect=center]  # not connected
  Pad43 = Pad [width=3.5794580238945084 height=1.453889245399575 connect=center]  # not connected
  Pad42 = Pad [width=3.5794580238945084 height=1.453889245399575 connect=center]  # not connected
  Pad41 = Pad [width=3.5794580238945084 height=1.453889245399575 connect=center]  # not connected
  Pad40 = Pad [width=3.5794580238945084 height=1.453889245399575 connect=center]  # not connected
  Pad39 = Pad [width=3.5794580238945084 height=1.453889245399575 connect=center]  # not connected
  Pad38 = Pad [width=3.5794580238945084 height=1.453889245399575 connect=center]  # not connected
  Pad37 = Pad [width=3.5794580238945084 height=1.453889245399575 connect=center]  # not connected
  Pad36 = Pad [width=3.5794580238945084 height=1.453889245399575 connect=center]  # not connected
  Pad33 = Pad [width=3.5794580238945084 height=1.453889245399575 connect=center]  # not connected
  Pad32 = Pad [width=3.5794580238945084 height=1.453889245399575 connect=center]  # not connected
  Pad31 = Pad [width=3.5794580238945084 height=1.453889245399575 connect=center]  # not connected
  Pad30 = Pad [width=3.5794580238945084 height=1.453889245399575 connect=center]  # not connected
  Pad29 = Pad [width=3.5794580238945084 height=1.453889245399575 connect=center]  # not connected
  Pad28 = Pad [width=3.5794580238945084 height=1.453889245399575 connect=center]  # not connected
  Pad27 = Pad [width=3.5794580238945084 height=1.453889245399575 connect=center]  # not connected
  Pad26 = Pad [width=3.5794580238945084 height=1.453889245399575 connect=center]  # not connected
  Pad25 = Pad [width=3.5794580238945084 height=1.453889245399575 connect=center]  # not connected
  Pad24 = Pad [width=3.5794580238945084 height=1.453889245399575 connect=center]  # not connected
  Pad23 = Pad [width=3.5794580238945084 height=1.453889245399575 connect=center]  # not connected
  Pad22 = Pad [width=3.5794580238945084 height=1.453889245399575 connect=center]  # not connected
  Pad21 = Pad [width=3.5794580238945084 height=1.453889245399575 connect=center]  # not connected
  Pad20 = Pad [width=3.5794580238945084 height=1.453889245399575 connect=center]  # not connected
  Pad19 = Pad [width=3.5794580238945084 height=1.453889245399575 connect=center]  # not connected
  Pad18 = Pad [width=3.5794580238945084 height=1.453889245399575 connect=center]  # not connected
  Pad17 = Pad [width=3.5794580238945084 height=1.453889245399575 connect=center]  # not connected
  Pad16 = Pad [width=3.5794580238945084 height=1.453889245399575 connect=center]  # not connected
  Pad15 = Pad [width=3.5794580238945084 height=1.453889245399575 connect=center]  # not connected
  Pad14 = Pad [width=3.5794580238945084 height=1.453889245399575 connect=center]  # not connected
  Pad13 = Pad [width=3.5794580238945084 height=1.453889245399575 connect=center]  # not connected
  Pad12 = Pad [width=3.5794580238945084 height=1.453889245399575 connect=center]  # not connected
  Pad11 = Pad [width=3.5794580238945084 height=1.453889245399575 connect=center]  # not connected
  Mod1 = Arduino Pro Mini wavgat
  test_switch = Toggle Switch [package=THT]
  S4 = Pushbutton [package="[THT]"]
  Q1 = Basic FET N-Channel [package="TO220 [THT]"]
  4_5V = female pin header, 2 pins [form="♀ (female)"]
  9V = female pin header, 2 pins [form="♀ (female)"]
  sensore_umidità = female pin header, 3 pins [form="♀ (female)"]
  sensore_temperatura = female pin header, 3 pins [form="♀ (female)"]
  R2 = Resistor Mini [tolerance=±5% resistance=100k package=THT]
  J1 = female pin header, 2 pins [form="♀ (female)"]
  D1 = Rectifier Diode [part_number=1N4001 package="300 mil [THT]"]
  C1 = Electrolytic Capacitor [capacitance=0.1mF voltage=35V package="100 mil [THT, electrolytic]"]
  Componente1 = RTC DS3231 for Raspberry Pi
  4_5V1 = male pin header, 5 pins [form="♂ (male)"]  # not connected
  R3 = Vertical Resistor [tolerance=±5% resistance=330 package=THT]
  R4 = Resistor Mini [tolerance=±5% resistance=4.7k package=THT]

nets:
  GND: Mod1.pin_4, Mod1.pin_23, Mod1.pin_26, test_switch.COM, S4.Pin_3, S4.Pin_4, Q1.source, 4_5V.pin1, 9V.pin2, sensore_umidità.pin3, sensore_temperatura.pin3, R2.Pin_1, C1.-, Componente1.-
  N1: Mod1.pin_5, sensore_temperatura.pin2
  N2: Mod1.pin_6, sensore_temperatura.pin1, R4.Pin_1
  PIN 10: Mod1.pin_13, R3.Pin_1
  N3: Mod1.pin_14, S4.Pin_1
  N4: Mod1.pin_17, test_switch.L1
  N5: Mod1.pin_19, sensore_umidità.pin2
  N6: Mod1.pin_20, sensore_umidità.pin1
  +4.5V: Mod1.pin_21, Mod1.pin_27, 4_5V.pin2, Componente1.+
  N7: Mod1.pin_31, Componente1.D
  N8: Mod1.pin_32, Componente1.C
  N9: Q1.gate, R2.Pin_0, R3.Pin_0
  N10: Q1.drain, J1.pin2, D1.anode
  +9V: 9V.pin1, J1.pin1, D1.cathode, C1.+

notes:
  A B C D E F G H I J K L M N O P Q R S T U V W X
  1  2  3  4  5  6  7  8  9 10 11 12 13 14 15 16 17 18
  18 17 16 15 14 13 12 11 10  9  8  7  6  5  4  3  2  1

custom parts:
  Arduino Pro Mini wavgat: Arduino Pro mini wavgat clone (note: there are many wavgat clones, so check that this one matches the actual board you have!)
  Resistor Mini: A generic resistor (0.25W)
  Rectifier Diode: A standard rectifier diode
  Vertical Resistor: A generic resistor (0.25W)
